# Fritzing sketch wiring (saved by Fritzing 1.0.4)

parts:
  U1 = XIAO ESP32C3
  OLED_I2C1 = OLED 128x64 I2C Monochrome Display
  Part1 = InvenSense MPU6050
  BAT1 = Battery Holders [package=lipo-1100mAh]  # not connected
  U3 = LIPO-110mAh [package=lipo-110]
  S2 = Pushbutton [package=THT]
  R1 = Resistor [tolerance=±5% resistance=220 package="0402 [SMD]"]  # not connected

nets:
  N1: U1.D1, S2.leg0
  N2: U1.D4, OLED_I2C1.SDA, Part1.SDA
  N3: U1.D5, OLED_I2C1.SCK, Part1.SCL
  GND: U1.GND, OLED_I2C1.GND, Part1.GND
  5V: U1.5V, OLED_I2C1.VDD, Part1.VCC
  N4: U3.-, S2.leg1

custom parts:
  XIAO ESP32C3: Seeed Studio XIAO ESP32C3 adopts new RISC-V architecture, supporting both Wi-Fi and BLE wireless connectivities. For Internet of Things applications, you will find it is flexible and suitable for all kinds of IoT scenarios.
